// Logisim project processor.circ as structural Verilog: 1 circuit, main circuit main
module main (
);

  wire and_1_out, and_2_out, button_1_out, clock_1_out, comparator_1_eq, comparator_1_gt, decoder_1_out0,
       decoder_1_out1, decoder_1_out2, decoder_1_out3, decoder_2_out0, decoder_2_out1, not_1_out, not_2_out,
       or_1_out;
  wire [1:0] controlled_buffer_11_out;
  wire [3:0] controlled_buffer_1_out;
  wire [5:0] controlled_buffer_5_out, controlled_buffer_6_out;
  wire [7:0] adder_1_out, bit_extender_1_out, controlled_buffer_7_out, controlled_buffer_8_out,
       controlled_buffer_12_out, controlled_buffer_13_out, counter_1_q, multiplexer_1_out, multiplexer_2_out,
       negator_1_out, PROGRAM_data, register_1_q, subtractor_1_out;

  ROM PROGRAM (.addr(counter_1_q), .data(PROGRAM_data));
  Counter counter_1 (.Q(counter_1_q), .clk(clock_1_out), .clr(button_1_out));  // open: load, D, count, carry, up
  Decoder #(.select(2)) decoder_1 (
    .out0(decoder_1_out0), .out1(decoder_1_out1), .out2(decoder_1_out2), .out3(decoder_1_out3),
    .sel(PROGRAM_data[1:0]));  // open: en
  assign controlled_buffer_1_out = decoder_1_out1 ? 4'b0110 : 4'bz;  // Controlled_Buffer controlled_buffer_1
  assign controlled_buffer_1_out = decoder_1_out0 ? 4'b0010 : 4'bz;  // Controlled_Buffer controlled_buffer_2
  assign controlled_buffer_1_out = decoder_1_out2 ? 4'b1000 : 4'bz;  // Controlled_Buffer controlled_buffer_3
  assign controlled_buffer_1_out = decoder_1_out3 ? 4'b0001 : 4'bz;  // Controlled_Buffer controlled_buffer_4
  Button button_1 (.out(button_1_out));
  Clock clock_1 (.out(clock_1_out));
  not not_1 (not_1_out, decoder_1_out3);
  assign controlled_buffer_5_out = not_1_out ? PROGRAM_data[7:2] : 6'bz;  // Controlled_Buffer controlled_buffer_5
  assign controlled_buffer_6_out = decoder_1_out3 ? PROGRAM_data[7:2] : 6'bz;  // Controlled_Buffer controlled_buffer_6
  assign controlled_buffer_7_out = controlled_buffer_1_out[3] ? bit_extender_1_out : 8'bz;  // Controlled_Buffer controlled_buffer_7
  assign bit_extender_1_out = {{2{1'b0}}, controlled_buffer_5_out};  // Bit_Extender bit_extender_1
  Decoder decoder_2 (.out0(decoder_2_out0), .out1(decoder_2_out1), .sel(controlled_buffer_6_out[0]));  // open: en
  Adder adder_1 (.a(register_1_q), .b(bit_extender_1_out), .out(adder_1_out));  // open: cin, cout
  Subtractor subtractor_1 (.a(register_1_q), .b(bit_extender_1_out), .out(subtractor_1_out));  // open: bin, bout
  Comparator comparator_1 (.a(register_1_q), .b({8{1'b0}}), .gt(comparator_1_gt), .eq(comparator_1_eq));  // open: lt
  assign controlled_buffer_8_out = controlled_buffer_1_out[2] ? subtractor_1_out : 8'bz;  // Controlled_Buffer controlled_buffer_8
  or or_1 (or_1_out, comparator_1_gt, comparator_1_eq);
  Negator negator_1 (.in(register_1_q), .out(negator_1_out));
  assign controlled_buffer_7_out = controlled_buffer_1_out[1] ? multiplexer_1_out : 8'bz;  // Controlled_Buffer controlled_buffer_9
  Register register_1 (
    .D(controlled_buffer_7_out), .clk(clock_1_out), .Q(register_1_q), .clr(button_1_out));  // open: en
  Multiplexer #(.width(8)) multiplexer_1 (
    .in0(adder_1_out), .in1(controlled_buffer_8_out), .out(multiplexer_1_out),
    .sel(controlled_buffer_1_out[2]));
  assign controlled_buffer_7_out = controlled_buffer_1_out[0] ? multiplexer_2_out : 8'bz;  // Controlled_Buffer controlled_buffer_10
  // Probe on register_1_q
  // Probe on register_1_q
  Multiplexer #(.select(2), .width(8)) multiplexer_2 (
    .in0(register_1_q), .in1(controlled_buffer_12_out), .in2(controlled_buffer_13_out),
    .out(multiplexer_2_out), .sel(controlled_buffer_11_out));  // open: in3
  assign controlled_buffer_11_out = or_1_out ? 2'b00 : 2'bz;  // Controlled_Buffer controlled_buffer_11
  assign controlled_buffer_12_out = decoder_2_out0 ? {8{1'b0}} : 8'bz;  // Controlled_Buffer controlled_buffer_12
  assign controlled_buffer_13_out = decoder_2_out1 ? negator_1_out : 8'bz;  // Controlled_Buffer controlled_buffer_13
  assign controlled_buffer_11_out = and_1_out ? 2'b01 : 2'bz;  // Controlled_Buffer controlled_buffer_14
  assign controlled_buffer_11_out = and_2_out ? 2'b10 : 2'bz;  // Controlled_Buffer controlled_buffer_15
  and and_1 (and_1_out, decoder_2_out0, not_2_out);
  and and_2 (and_2_out, decoder_2_out1, not_2_out);
  not not_2 (not_2_out, or_1_out);

  // Notes on the sheet:
  //   PC
  //   contents of PROGRAM (hex, n*v repeats v):
  //   86 8 79 13*0 12
  //   a | IMM OUT
  //   c | ALU OUT
  //   b | ALU SUBTRACT
  //   d | ABS / RELU OUT
  //   Control signals
  //   set by opcode
  //   d
  //   c
  //   b
  //   a
  //   Reset
  //   Clock
  //   Selected Control Bits
  //   RELU 0 | 1 Abs
  //   Register Read
  //   Register Write
  //   REG
  //   REG Value
endmodule
